# Fritzing sketch Board_1 (saved by Fritzing 0.9.2b)
breadboards: 1

parts:
  Bauteil1 = BH1750
  DHT1 = DHT22 Humidity and Temperature Sensor
  PIR1 = PIR sensor
  LED1 = RGB LED (com. anode, rbg) [package="5 mm [THT]"]
  LED2 = LED - 5mm [color="Yellow (595nm)" package="5 mm [THT]"]
  S1 = Momentary Switch [package=ksa_sealed_tac_switch]
  R1 = Resistor [tolerance=±5% resistance=220 package="0402 [SMD]"]
  M1 = DOIT Esp32 DevKit v1 (30 pins long, 11 pins width) [part_number=ESP32S-PIN30]
  R3 = Resistor [tolerance=±5% resistance=220 package="0402 [SMD]"]
  R4 = Resistor [tolerance=±5% resistance=220 package="0402 [SMD]"]
  R5 = Resistor [tolerance=±5% resistance=220 package="0402 [SMD]"]
  R6 = Resistor [tolerance=±1% resistance=10k package=THT]

nets:
  N1: Bauteil1.VCC, S1.2
  GND: Bauteil1.GND, DHT1.GND, PIR1.GND, LED2.cathode, M1.GND, R6.Pin_1
  N2: Bauteil1.SCL, M1.D21
  N3: Bauteil1.SDA, M1.D22
  VDD: DHT1.VDD, PIR1.VDD, LED1.common_anode, M1.VIN
  N4: DHT1.DATA, M1.D14
  N5: PIR1.SIG, M1.D13
  N6: LED1.red_cathode, R5.Pin_0
  N7: LED1.blue_cathode, R4.Pin_0
  N8: LED1.green_cathode, R3.Pin_0
  N9: LED2.anode, R1.Pin_0
  N10: S1.3, M1.D33
  N11: S1.4, R6.Pin_0
  N12: R1.Pin_1, M1.G17
  N13: M1.D25, R5.Pin_1
  N14: M1.D26, R4.Pin_1
  N15: M1.D27, R3.Pin_1

notes:
  VCC,Data,GND
  R,VCC,G,B
  33
  25
  26
  27
  14
  13
  VCC
  22
  21
  17
  GND
  3V3

custom parts:
  BH1750: Light Sensor
  DOIT Esp32 DevKit v1 (30 pins long, 11 pins width): The DOIT Esp32 DevKit v1 is one of the development board created by DOIT to evaluate the ESP-WROOM-32 module. It is based on the ESP32 microcontroller that boasts Wifi, Bluetooth, Ethernet and Low Power support all in a single chip. (vanepp) made breadboard work, adjusted pin numbering and labels and reduced size of schematic and cleaned up pcb. This chip is 30pins long (2 x15) and 11 pins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
