# Fritzing sketch Board_2 (saved by Fritzing 0.9.2b)
breadboards: 1

parts:
  Bauteil1 = BH1750
  PIR1 = PIR sensor
  LED2 = LED - 5mm [color="Red (635nm)" package="5 mm [THT]"]
  R1 = Resistor [tolerance=±5% resistance=220 package="0402 [SMD]"]
  M1 = DOIT Esp32 DevKit v1 (30 pins long, 11 pins width) [part_number=ESP32S-PIN30]
  LED3 = LED - 5mm [color="Green (565nm)" package="5 mm [THT]"]
  R2 = Resistor [tolerance=±5% resistance=220 package="0402 [SMD]"]

nets:
  VCC: Bauteil1.VCC, M1.3V3
  GND: Bauteil1.GND, PIR1.GND, LED2.cathode, M1.GND, LED3.cathode
  N1: Bauteil1.SCL, M1.D21
  N2: Bauteil1.SDA, M1.D22
  VDD: PIR1.VDD, M1.VIN
  N3: PIR1.SIG, M1.D13
  N4: LED2.anode, R1.Pin_0
  N5: R1.Pin_1, M1.G17
  N6: M1.D18, R2.Pin_1
  N7: LED3.anode, R2.Pin_0

notes:
  13
  VCC
  VCC,Data,GND
  22
  21
  18
  17
  GND
  3V3

custom parts:
  BH1750: Light Sensor
  DOIT Esp32 DevKit v1 (30 pins long, 11 pins width): The DOIT Esp32 DevKit v1 is one of the development board created by DOIT to evaluate the ESP-WROOM-32 module. It is based on the ESP32 microcontroller that boasts Wifi, Bluetooth, Ethernet and Low Power support all in a single chip. (vanepp) made breadboard work, adjusted pin numbering and labels and reduced size of schematic and cleaned up pcb. This chip is 30pins long (2 x15) and 11 pins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
